# Fritzing sketch Схема!!!! (saved by Fritzing 0.9.10b)
breadboards: 1

parts:
  U1 = L9110 H-bridge module [part_number="L9110 H-bridge"]
  S1 = Water Pump [part_number=12V package=Pump]  # not connected
  A1 = 2 channel relay module [package=THT]
  Компонент1 = Arduino Uno (Rev3)
  Компонент2 = Arduino Nano (Rev3.0)
  HC-SR04_Sensor_1 = HC-SR04 Ultrasonic Distance Sensor
  HC-SR04_Sensor_2 = HC-SR04 Ultrasonic Distance Sensor
  S2 = Water Pump [part_number=12V package=Pump]  # not connected
  J1 = Basic Servo
  J2 = Basic Servo
  SM1 = 28BYJ-48 Stepper Motor [part_number=28BYJ-48]
  Driver1 = 28BYJ-48 Driver Module [part_number=ULN2003 package=THT]
  Power_plug1 = Power plug
  M1 = DC Motor [voltage_(max)=6V voltage_(min)=3V]

nets:
  N1: U1.B-IA, Компонент2.D5
  N2: U1.B-IB, Компонент2.D4
  GND: U1.GND, A1.pin_14, Компонент1.GND, Компонент2.GND, HC-SR04_Sensor_1.GND, HC-SR04_Sensor_2.GND, J1.gnd, J2.gnd, Driver1.GND, Power_plug1.GND
  VCC: U1.VCC, A1.pin_2, A1.pin_5, A1.pin_13, HC-SR04_Sensor_1.VCC, HC-SR04_Sensor_2.VCC, J1.vcc, J2.vcc, Driver1.Vmotor, Power_plug1.VCC
  N3: U1.MOTOR_B-A, M1.pin_2
  N4: U1.MOTOR_B-B, M1.pin_1
  N5: A1.pin_15, Компонент1.D8
  N6: A1.pin_16, Компонент1.D9_PWM
  N7: Компонент1.D10_PWM/SS, HC-SR04_Sensor_1.ECHO
  N8: Компонент1.D11_PWM/MOSI, HC-SR04_Sensor_1.TRIG
  N9: Компонент2.D2, HC-SR04_Sensor_2.ECHO
  N10: Компонент2.D3, HC-SR04_Sensor_2.TRIG
  N11: SM1.blue-pin, Driver1.blue-pin
  N12: SM1.pink-pin, Driver1.pink-pin
  N13: SM1.yellow-pin, Driver1.yellow-pin
  N14: SM1.orange-pin, Driver1.orange-pin
  N15: SM1.red-pin, Driver1.red-pin

custom parts:
  Water Pump: A Water Pump DC 12V
  2 channel relay module: 2 channel Relay Module 5V 12V 24V High and Low Level Trigger Relay Control With Optocoupler Two Way relays DC 5 V 12 V 24 V Volt.
  28BYJ-48 Stepper Motor: Unipolar Stepper Motor 28BYJ-48 Top coil - pink & orange Bottom coil - blue & yellow Common rail - red Connector pins: blue - pink - yellow - orange - red
  28BYJ-48 Driver Module: Generic male header
